# Fritzing sketch cakeExtruderSchematic (saved by Fritzing 0.9.3b)
breadboards: 1

parts:
  high_current_H-bridge_driver = A4950 [package=soicn]
  part = Arduino Uno (Rev3) - ICSP
  M1 = DC Motor
  motor_position_pot = Rotary Potentiometer (Large) [maximum_resistance=10kΩ package=THT]
  ABB_24V_control_signal = AC Power [voltage=24 frequency=60]
  part_2 = Resistor [tolerance=±5% resistance=4.7k package="0603 [SMD]"]
  part_3 = Resistor [tolerance=±5% resistance=1.5k package="0603 [SMD]"]

nets:
  N1: high_current_H-bridge_driver.IN2, part.D5_PWM
  N2: high_current_H-bridge_driver.IN1, part.D6_PWM
  12V: high_current_H-bridge_driver.VBB
  N3: high_current_H-bridge_driver.OUT1, M1.pin_1
  N4: high_current_H-bridge_driver.OUT2, M1.pin_2
  N5: part.A0, motor_position_pot.wiper
  N6: part.5V, motor_position_pot.leg2
  N7: part.D8, part_3.Pin_0
  N8: part.GND, motor_position_pot.leg1
  N9: ABB_24V_control_signal.V-, part_2.Pin_1, part_3.Pin_1
  GND: part_2.Pin_0
